// Logisim project ЗАЩИТА Дешифр .circ as structural Verilog: 1 circuit, main circuit main
module main (
  input  in_1,
  input  in_2,
  input  in_3,
  input  in_4,
  output out_5,
  output out_6,
  output out_7,
  output out_8,
  output out_9,
  output out_10,
  output out_11,
  output out_12
);

  wire nand_1_out, nand_2_out, nand_3_out;

  nand nand_1 (nand_1_out, in_1, in_1);
  nand nand_2 (nand_2_out, in_2, in_2);
  nand nand_3 (nand_3_out, in_3, in_3);
  nand nand_4 (out_5, nand_1_out, nand_2_out, nand_3_out, in_4);
  nand nand_5 (out_6, nand_1_out, nand_2_out, in_3, in_4);
  nand nand_6 (out_7, nand_1_out, in_2, nand_3_out, in_4);
  nand nand_7 (out_8, nand_1_out, in_2, in_3, in_4);
  nand nand_8 (out_9, in_1, nand_2_out, nand_3_out, in_4);
  nand nand_9 (out_10, in_1, nand_2_out, in_3, in_4);
  nand nand_10 (out_11, in_1, in_2, nand_3_out, in_4);
  nand nand_11 (out_12, in_1, in_2, in_3, in_4);
endmodule
