// Logisim project Триггеры.circ as structural Verilog: 1 circuit, main circuit main
module main (
  input  \не_S ,
  input  \не_S_2 ,
  input  C,
  input  \не_R ,
  input  \не_R_2 ,
  input  R,
  input  \не_S_3 ,
  input  S,
  input  C_2,
  input  \не_R_3 ,
  input  S_2,
  input  C_3,
  input  R_2,
  input  \не_S_4 ,
  input  T,
  input  \не_S_5 ,
  input  S_3,
  input  \не_R_4 ,
  input  C_4,
  input  R_3,
  input  \не_S_6 ,
  input  \не_R_5 ,
  input  J,
  input  D,
  input  C_5,
  input  C_6,
  input  K,
  input  \не_R_6 ,
  output Q,
  output Q_2,
  output \не_Q ,
  output \не_Q_2 ,
  output Q_3,
  output Q_4,
  output \не_Q_3 ,
  output \не_Q_4 ,
  output Q_5,
  output \не_Q_5 ,
  output Q_6,
  output \не_Q_6 ,
  output Q_7,
  output \не_Q_7 ,
  output Q_8,
  output Q_9,
  output \не_Q_8 ,
  output \не_Q_9 
);

  wire nand_3_out, nand_4_out, nand_5_out, nand_6_out, nand_7_out, nand_8_out, nand_11_out, nand_12_out,
       nand_13_out, nand_16_out, nand_17_out, nand_18_out, nand_21_out, nand_22_out, nand_23_out,
       nand_24_out, nand_25_out, nand_26_out, nand_27_out, nand_28_out, nand_29_out, nand_30_out,
       nand_31_out, nand_32_out, nand_33_out, nand_36_out, nand_37_out, nand_38_out, nand_39_out, nor_3_out,
       nor_4_out, nor_5_out, nor_6_out;

  nand nand_1 (Q, \не_S , \не_Q );
  nand nand_2 (\не_Q , Q, \не_R );
  nor nor_1 (Q_3, R, \не_Q_3 );
  nor nor_2 (\не_Q_3 , Q_3, S);
  nand nand_3 (nand_3_out, S_2, C_3);
  nand nand_4 (nand_4_out, C_3, R_2);
  nand nand_5 (nand_5_out, S_3, nand_6_out);
  nand nand_6 (nand_6_out, C_4, C_4);
  nand nand_7 (nand_7_out, nand_6_out, R_3);
  nand nand_8 (nand_8_out, D, D);
  nand nand_9 (Q_5, nand_3_out, \не_Q_5 );
  nand nand_10 (\не_Q_5 , Q_5, nand_4_out);
  nand nand_11 (nand_11_out, \не_S_5 , nand_5_out, nand_12_out);
  nand nand_12 (nand_12_out, nand_11_out, nand_7_out, \не_R_5 );
  nand nand_13 (nand_13_out, D, C_6);
  nand nand_14 (Q_9, nand_13_out, \не_Q_9 );
  nand nand_15 (\не_Q_9 , Q_9, nand_16_out);
  nand nand_16 (nand_16_out, C_6, nand_8_out);
  nand nand_17 (nand_17_out, nand_11_out, C_4);
  nand nand_18 (nand_18_out, C_4, nand_12_out);
  nand nand_19 (Q_7, \не_S_5 , nand_17_out, \не_Q_7 );
  nand nand_20 (\не_Q_7 , Q_7, nand_18_out, \не_R_5 );
  nand nand_21 (nand_21_out, \не_S_2 , nand_24_out);
  nand nand_22 (nand_22_out, nand_25_out, \не_R_2 );
  nor nor_3 (nor_3_out, \не_S_3 , nor_5_out);
  nor nor_4 (nor_4_out, nor_6_out, \не_R_3 );
  nand nand_23 (nand_23_out, T, T);
  nand nand_24 (nand_24_out, nand_25_out, nand_21_out, C);
  nand nand_25 (nand_25_out, C, nand_22_out, nand_24_out);
  nor nor_5 (nor_5_out, nor_6_out, nor_3_out, C_2);
  nor nor_6 (nor_6_out, C_2, nor_4_out, nor_5_out);
  nand nand_26 (nand_26_out, \не_Q_6 , nand_23_out);
  nand nand_27 (nand_27_out, nand_23_out, Q_6);
  nand nand_28 (nand_28_out, \не_Q_8 , J, C_5);
  nand nand_29 (nand_29_out, C_5, K, Q_8);
  nand nand_30 (nand_30_out, \не_S_4 , nand_26_out, nand_31_out);
  nand nand_31 (nand_31_out, nand_30_out, nand_27_out, \не_R_4 );
  nand nand_32 (nand_32_out, \не_S_6 , nand_28_out, nand_33_out);
  nand nand_33 (nand_33_out, nand_32_out, nand_29_out, \не_R_6 );
  nand nand_34 (Q_2, nand_24_out, \не_Q_2 );
  nand nand_35 (\не_Q_2 , Q_2, nand_25_out);
  nor nor_7 (Q_4, nor_5_out, \не_Q_4 );
  nor nor_8 (\не_Q_4 , Q_4, nor_6_out);
  nand nand_36 (nand_36_out, nand_30_out, T);
  nand nand_37 (nand_37_out, T, nand_31_out);
  nand nand_38 (nand_38_out, nand_32_out, nand_28_out, nand_29_out);
  nand nand_39 (nand_39_out, nand_29_out, nand_28_out, nand_33_out);
  nand nand_40 (Q_6, \не_S_4 , nand_36_out, \не_Q_6 );
  nand nand_41 (\не_Q_6 , Q_6, nand_37_out, \не_R_4 );
  nand nand_42 (Q_8, \не_S_6 , \не_Q_8 , nand_38_out);
  nand nand_43 (\не_Q_8 , nand_39_out, Q_8, \не_R_6 );
endmodule
