// Logisim project ЗАЩИТА Преобразователь кодов.circ as structural Verilog: 1 circuit, main circuit main
module main (
  input  in_1,
  input  in_2,
  input  in_3,
  input  in_4,
  output out_5,
  output out_6,
  output out_7,
  output out_8,
  output out_9,
  output out_10,
  output out_11,
  output out_12
);

  wire decoder_1_out0, decoder_1_out1, decoder_1_out2, decoder_1_out3, decoder_1_out4, decoder_1_out5,
       decoder_1_out6, decoder_1_out7, decoder_1_out8, decoder_1_out9, decoder_1_out10, decoder_1_out11,
       decoder_1_out12, decoder_1_out13, decoder_1_out14, decoder_1_out15, or_1_out, or_2_out, or_3_out,
       or_4_out, or_5_out, or_6_out, or_7_out, or_8_out, or_9_out, or_10_out, or_11_out, or_12_out,
       or_13_out, or_14_out, or_15_out;

  Hex_Digit_Display hex_digit_display_1 (.value({out_12, out_11, out_10, out_9}));  // open: dp
  Hex_Digit_Display hex_digit_display_2 (.value({out_8, out_7, out_6, out_5}));  // open: dp
  Decoder #(.select(4), .enable("false")) decoder_1 (
    .out0(decoder_1_out0), .out1(decoder_1_out1), .out2(decoder_1_out2), .out3(decoder_1_out3),
    .out4(decoder_1_out4), .out5(decoder_1_out5), .out6(decoder_1_out6), .out7(decoder_1_out7),
    .out8(decoder_1_out8), .out9(decoder_1_out9), .out10(decoder_1_out10), .out11(decoder_1_out11),
    .out12(decoder_1_out12), .out13(decoder_1_out13), .out14(decoder_1_out14), .out15(decoder_1_out15),
    .sel({in_1, in_2, in_3, in_4}));
  or or_1 (or_1_out, decoder_1_out0, decoder_1_out13);
  or or_2 (or_2_out, decoder_1_out1, decoder_1_out14);
  or or_3 (or_3_out, decoder_1_out2, decoder_1_out15);
  buf or_4 (or_4_out, decoder_1_out4);  // OR_Gate
  buf or_5 (or_5_out, decoder_1_out3);  // OR_Gate
  buf or_6 (or_6_out, decoder_1_out5);  // OR_Gate
  buf or_7 (or_7_out, decoder_1_out6);  // OR_Gate
  buf or_8 (or_8_out, decoder_1_out8);  // OR_Gate
  buf or_9 (or_9_out, decoder_1_out7);  // OR_Gate
  buf or_10 (or_10_out, decoder_1_out9);  // OR_Gate
  buf or_11 (or_11_out, decoder_1_out10);  // OR_Gate
  buf or_12 (or_12_out, decoder_1_out12);  // OR_Gate
  buf or_13 (or_13_out, decoder_1_out11);  // OR_Gate
  Priority_Encoder #(.select(4)) priority_encoder_1 (
    .in0(or_1_out), .in1(or_2_out), .in2(or_3_out), .in3(or_5_out), .in4(or_4_out), .in5(or_6_out),
    .in6(or_7_out), .in7(or_9_out), .in8(or_8_out), .in9(or_10_out), .in10(or_11_out), .in11(or_13_out),
    .in12(or_12_out), .out({out_8, out_7, out_6, out_5}));  // open: in13, in14, in15, gs, en_out, en_in
  or or_14 (or_14_out, decoder_1_out0, decoder_1_out1, decoder_1_out2, decoder_1_out3, decoder_1_out4, decoder_1_out5, decoder_1_out6, decoder_1_out7, decoder_1_out8, decoder_1_out9, decoder_1_out10, decoder_1_out11, decoder_1_out12);
  or or_15 (or_15_out, decoder_1_out15, decoder_1_out14, decoder_1_out13);
  Priority_Encoder #(.select(4)) priority_encoder_2 (
    .in0(or_14_out), .in1(or_15_out), .out({out_12, out_11, out_10, out_9}));  // open: in2, in3, in4, in5, in6, in7, in8, in9, in10, in11, in12, in13, in14, in15, gs, en_out, en_in
endmodule
